# Fritzing sketch Schéma capteur distance + LCD (saved by Fritzing 0.9.3b)

parts:
  Composant1 = Arduino Uno (Rev3)
  hc-sr1 = hc-sr04
  Grove1 = Grove OLED 128x96

nets:
  N1: Composant1.A4/SDA, Grove1.SDA
  N2: Composant1.A5/SCL, Grove1.SCL
  N3: Composant1.D11_PWM/MOSI, hc-sr1.Echo
  N4: Composant1.D12/MISO, hc-sr1.Trig
  VCC: Composant1.5V, hc-sr1.VCC, Grove1.VCC
  GND: Composant1.GND, hc-sr1.GND, Grove1.GND

custom parts:
  hc-sr04: This is a HC-SR04 Distance Sensor
