# Fritzing sketch Schéma capteur distance (saved by Fritzing 0.9.3b)

parts:
  Composant1 = Arduino Uno (Rev3)
  hc-sr1 = hc-sr04

nets:
  N1: Composant1.D11_PWM/MOSI, hc-sr1.Echo
  N2: Composant1.D12/MISO, hc-sr1.Trig
  GND: Composant1.GND, hc-sr1.GND
  5V: Composant1.5V, hc-sr1.VCC
