# Fritzing sketch Schéma écran LCD (saved by Fritzing 0.9.3b)

parts:
  Composant1 = Arduino Uno (Rev3)
  Grove1 = Grove OLED 128x96

nets:
  N1: Composant1.A4/SDA, Grove1.SDA
  N2: Composant1.A5/SCL, Grove1.SCL
  GND: Composant1.GND, Grove1.GND
  5V: Composant1.5V, Grove1.VCC
